// Logisim project alu.circ as structural Verilog: 4 circuits, main circuit ALU
module ALU (
  input  [31:0] X,
  input  [31:0] Y,
  input  [3:0] AluOP,
  output Signed_Overflow,
  output UnSigned_Overflow,
  output Equal,
  output [31:0] Result,
  output [31:0] Result_2
);

  wire adder32_1_cf, adder32_1_of, adder32_2_of, comparator_1_lt, comparator_2_lt, comparator_3_gt, not_2_out;
  wire [31:0] adder32_1_out_4, adder32_2_out_4, and_1_out, bit_extender_1_out, bit_extender_2_out,
       bit_extender_3_out, divider_1_out, divider_1_rem, multiplier_1_cout, multiplier_1_out, nor_1_out,
       not_1_out, or_1_out, shifter_1_out, shifter_2_out, shifter_3_out, shifter_4_out, shifter_5_out,
       xor_1_out;

  // Probe on X
  // Probe on X
  // Probe on Y
  // Probe on Y
  Shifter #(.width(32)) shifter_1 (.in(X), .\dist (Y[4:0]), .out(shifter_1_out));
  Shifter #(.width(32), .shift("ar")) shifter_2 (.in(X), .\dist (Y[4:0]), .out(shifter_2_out));
  Shifter #(.width(32), .shift("lr")) shifter_3 (.in(X), .\dist (Y[4:0]), .out(shifter_3_out));
  Multiplier #(.width(32)) multiplier_1 (.a(X), .b(Y), .out(multiplier_1_out), .cout(multiplier_1_cout));  // open: cin
  Divider #(.width(32)) divider_1 (.a(X), .b(Y), .out(divider_1_out), .rem(divider_1_rem));  // open: upper
  adder32 adder32_1 (.Cin(1'b0), .A(X), .B(Y), .out_4(adder32_1_out_4), .CF(adder32_1_cf), .OF(adder32_1_of));
  adder32 adder32_2 (.Cin(1'b1), .A(X), .B(not_1_out), .out_4(adder32_2_out_4), .OF(adder32_2_of));  // open: CF
  assign not_1_out = ~Y;  // NOT_Gate not_1, 32 bits wide
  assign and_1_out = X & Y;  // AND_Gate and_1, 32 bits wide
  assign or_1_out = X | Y;  // OR_Gate or_1, 32 bits wide
  assign xor_1_out = X ^ Y;  // XOR_Gate xor_1, 32 bits wide
  assign nor_1_out = ~(X | Y);  // NOR_Gate nor_1, 32 bits wide
  Comparator #(.width(32)) comparator_1 (.a(X), .b(Y), .lt(comparator_1_lt));  // open: gt, eq
  Comparator #(.width(32), .mode("unsigned")) comparator_2 (
    .a(X), .b(Y), .eq(Equal), .lt(comparator_2_lt));  // open: gt
  Shifter #(.width(32)) shifter_4 (.in(Y), .\dist (X[4:0]), .out(shifter_4_out));
  Shifter #(.width(32), .shift("ar")) shifter_5 (.in(Y), .\dist (X[4:0]), .out(shifter_5_out));
  Comparator #(.width(32)) comparator_3 (.a(X), .b({32{1'b0}}), .gt(comparator_3_gt));  // open: eq, lt
  // Probe on AluOP
  not not_2 (not_2_out, comparator_3_gt);
  // Probe on Result
  // Probe on Result
  assign bit_extender_1_out = {{31{1'b0}}, comparator_1_lt};  // Bit_Extender bit_extender_1
  assign bit_extender_2_out = {{31{1'b0}}, comparator_2_lt};  // Bit_Extender bit_extender_2
  assign bit_extender_3_out = {{31{1'b0}}, not_2_out};  // Bit_Extender bit_extender_3
  // Probe on Result_2
  Multiplexer #(.select(4), .width(32), .enable("false")) multiplexer_1 (
    .in0(shifter_1_out), .in1(shifter_2_out), .in2(shifter_3_out), .in3(multiplier_1_out),
    .in4(divider_1_out), .in5(adder32_1_out_4), .in6(adder32_2_out_4), .in7(and_1_out), .in8(or_1_out),
    .in9(xor_1_out), .in10(nor_1_out), .in11(bit_extender_1_out), .in12(bit_extender_2_out),
    .in13(shifter_4_out), .in14(shifter_5_out), .in15(bit_extender_3_out), .out(Result), .sel(AluOP));
  Multiplexer #(.select(4), .width(32), .enable("false")) multiplexer_2 (
    .in0({32{1'b0}}), .in1({32{1'b0}}), .in2({32{1'b0}}), .in3(multiplier_1_cout), .in4(divider_1_rem),
    .in5({32{1'b0}}), .in6({32{1'b0}}), .in7({32{1'b0}}), .in8({32{1'b0}}), .in9({32{1'b0}}),
    .in10({32{1'b0}}), .in11({32{1'b0}}), .in12({32{1'b0}}), .in13({32{1'b0}}), .in14({32{1'b0}}),
    .in15({32{1'b0}}), .out(Result_2), .sel(AluOP));
  Multiplexer #(.select(4), .enable("false")) multiplexer_3 (
    .in0(1'b0), .in1(1'b0), .in2(1'b0), .in3(1'b0), .in4(1'b0), .in5(adder32_1_of), .in6(adder32_2_of),
    .in7(1'b0), .in8(1'b0), .in9(1'b0), .in10(1'b0), .in11(1'b0), .in12(1'b0), .in13(1'b0), .in14(1'b0),
    .in15(1'b0), .out(Signed_Overflow), .sel(AluOP));
  Multiplexer #(.select(4), .enable("false")) multiplexer_4 (
    .in0(1'b0), .in1(1'b0), .in2(1'b0), .in3(1'b0), .in4(1'b0), .in5(adder32_1_cf), .in6(comparator_2_lt),
    .in7(1'b0), .in8(1'b0), .in9(1'b0), .in10(1'b0), .in11(1'b0), .in12(1'b0), .in13(1'b0), .in14(1'b0),
    .in15(1'b0), .out(UnSigned_Overflow), .sel(AluOP));

  // Other names for the same wires on the sheet: CF = UnSigned_Overflow; OF = Signed_Overflow;
  //   Result2[31:0] = Result_2; S[3:0] = AluOP

  // Notes on the sheet:
  //   不要改变此引脚区域内容，也不要改变ALU封装形式
  //   输入引脚
  //   请在下方利用上方输入输出引脚的隧道信号构建ALU电路，ctrl+d复制选择部件
  //   输出引脚
  //   探测区域
endmodule

module adder4 (
  input  Cin,
  input  [3:0] A,
  input  [3:0] B,
  output [3:0] S,
  output P,
  output G
);

  wire and_1_out, and_2_out, and_3_out, and_4_out, and_5_out, and_6_out, and_7_out, and_8_out, and_9_out,
       and_10_out, buffer_1_out, buffer_2_out, buffer_3_out, buffer_4_out, nand_1_out, nand_2_out,
       nand_3_out, nand_4_out, nor_1_out, nor_2_out, nor_3_out, nor_4_out, nor_6_out, nor_7_out, nor_8_out,
       not_1_out, not_2_out, or_1_out, or_2_out, or_3_out;

  not not_1 (not_1_out, Cin);
  nand nand_1 (nand_1_out, A[0], B[0]);
  nor nor_1 (nor_1_out, A[0], B[0]);
  nand nand_2 (nand_2_out, A[1], B[1]);
  nor nor_2 (nor_2_out, A[1], B[1]);
  nand nand_3 (nand_3_out, A[2], B[2]);
  nor nor_3 (nor_3_out, A[2], B[2]);
  nand nand_4 (nand_4_out, A[3], B[3]);
  nor nor_4 (nor_4_out, A[3], B[3]);
  buf buffer_1 (buffer_1_out, nor_1_out);
  buf buffer_2 (buffer_2_out, nor_2_out);
  buf buffer_3 (buffer_3_out, nor_3_out);
  buf buffer_4 (buffer_4_out, nand_4_out);
  not not_2 (not_2_out, not_1_out);
  and and_1 (and_1_out, nand_1_out, ~nor_1_out);  // AND_Gate
  and and_2 (and_2_out, not_1_out, nand_1_out);
  and and_3 (and_3_out, nand_2_out, ~nor_2_out);  // AND_Gate
  and and_4 (and_4_out, not_1_out, nand_1_out, nand_2_out);
  and and_5 (and_5_out, nand_2_out, nor_1_out);
  and and_6 (and_6_out, nand_3_out, ~nor_3_out);  // AND_Gate
  and and_7 (and_7_out, not_1_out, nand_1_out, nand_2_out, nand_3_out);
  and and_8 (and_8_out, nand_2_out, nand_3_out, nor_1_out);
  and and_9 (and_9_out, nand_3_out, nor_2_out);
  and and_10 (and_10_out, nand_4_out, ~nor_4_out);  // AND_Gate
  nor nor_5 (P, nor_1_out, nor_2_out, nor_3_out, nor_4_out);
  or or_1 (or_1_out, nor_1_out, nor_2_out, nor_3_out, nor_4_out, nand_1_out);
  or or_2 (or_2_out, nor_3_out, nor_4_out, nand_2_out);
  or or_3 (or_3_out, nor_4_out, nand_3_out);
  nor nor_6 (nor_6_out, and_2_out, buffer_1_out);
  nor nor_7 (nor_7_out, and_4_out, and_5_out, buffer_2_out);
  nor nor_8 (nor_8_out, and_7_out, and_8_out, and_9_out, buffer_3_out);
  nand nand_5 (G, or_1_out, or_2_out, or_3_out, buffer_4_out);
  xor xor_1 (S[0], not_2_out, and_1_out);
  xor xor_2 (S[1], nor_6_out, and_3_out);
  xor xor_3 (S[2], nor_7_out, and_6_out);
  xor xor_4 (S[3], nor_8_out, and_10_out);
endmodule

module adder16 (
  input  Cin,
  input  [15:0] A,
  input  [15:0] B,
  output [15:0] S,
  output P,
  output G
);

  wire adder4_1_g, adder4_1_p, adder4_2_g, adder4_2_p, adder4_3_g, adder4_3_p, adder4_4_g, adder4_4_p,
       and_1_out, and_2_out, and_3_out, and_4_out, and_5_out, and_6_out, and_7_out, and_8_out, and_9_out,
       or_1_out, or_2_out, or_3_out;

  adder4 adder4_1 (.Cin(Cin), .A(A[3:0]), .B(B[3:0]), .S(S[3:0]), .P(adder4_1_p), .G(adder4_1_g));
  adder4 adder4_2 (.Cin(or_1_out), .A(A[7:4]), .B(B[7:4]), .S(S[7:4]), .P(adder4_2_p), .G(adder4_2_g));
  adder4 adder4_3 (.Cin(or_2_out), .A(A[11:8]), .B(B[11:8]), .S(S[11:8]), .P(adder4_3_p), .G(adder4_3_g));
  adder4 adder4_4 (.Cin(or_3_out), .A(A[15:12]), .B(B[15:12]), .S(S[15:12]), .P(adder4_4_p), .G(adder4_4_g));
  and and_1 (and_1_out, adder4_1_p, Cin);
  and and_2 (and_2_out, adder4_2_p, adder4_1_g);
  and and_3 (and_3_out, adder4_2_p, adder4_1_p, Cin);
  and and_4 (and_4_out, adder4_3_p, adder4_2_g);
  and and_5 (and_5_out, adder4_3_p, adder4_2_p, adder4_1_g);
  and and_6 (and_6_out, adder4_3_p, adder4_2_p, adder4_1_p, Cin);
  and and_7 (and_7_out, adder4_4_p, adder4_3_g);
  and and_8 (and_8_out, adder4_4_p, adder4_3_p, adder4_2_g);
  and and_9 (and_9_out, adder4_4_p, adder4_3_p, adder4_2_p, adder4_1_g);
  and and_10 (P, adder4_4_p, adder4_3_p, adder4_2_p, adder4_1_p, Cin);
  or or_1 (or_1_out, adder4_1_g, and_1_out);
  or or_2 (or_2_out, adder4_2_g, and_2_out, and_3_out);
  or or_3 (or_3_out, adder4_3_g, and_4_out, and_5_out, and_6_out);
  or or_4 (G, adder4_4_g, and_7_out, and_8_out, and_9_out);
endmodule

module adder32 (
  input  Cin,
  input  [31:0] A,
  input  [31:0] B,
  output [31:0] out_4,
  output CF,
  output OF
);

  wire adder16_1_g, adder16_1_p, adder16_2_g, adder16_2_p, and_1_out, and_2_out, and_3_out, and_4_out,
       and_5_out, or_1_out;

  adder16 adder16_1 (.Cin(Cin), .A(A[15:0]), .B(B[15:0]), .S(out_4[15:0]), .P(adder16_1_p), .G(adder16_1_g));
  adder16 adder16_2 (.Cin(or_1_out), .A(A[31:16]), .B(B[31:16]), .S(out_4[31:16]), .P(adder16_2_p), .G(adder16_2_g));
  and and_1 (and_1_out, adder16_1_p, Cin);
  and and_2 (and_2_out, adder16_2_p, adder16_1_g);
  and and_3 (and_3_out, adder16_2_p, adder16_1_p, Cin);
  or or_1 (or_1_out, adder16_1_g, and_1_out);
  or or_2 (CF, adder16_2_g, and_2_out, and_3_out);
  and and_4 (and_4_out, ~out_4[31], A[31], B[31]);  // AND_Gate
  and and_5 (and_5_out, out_4[31], ~A[31], ~B[31]);  // AND_Gate
  or or_3 (OF, and_4_out, and_5_out);
endmodule
