// Logisim project mips_cpu.circ as structural Verilog: 21 circuits, main circuit CPU
module IR_circle (
  input  [31:0] \input ,
  output RegDst,
  output Branch,
  output Jump,
  output MemToReg,
  output MemRead,
  output MemWrite,
  output AluSrc,
  output RegWrite,
  output [3:0] ALU_op,
  output X_src_R2,
  output JAL,
  output jr,
  output syscall,
  output mfc0,
  output mtc0,
  output eret,
  output [1:0] Branch_sel,
  output lh
);

  wire ir_2_1_regwrite, ir_3_1_alusc;
  wire [2:0] ir_4_1_aluop2;

  ir_1 ir_1_1 (
    .op1(\input [31]), .op2(\input [30]), .op3(\input [29]), .op4(\input [28]), .op5(\input [27]),
    .op6(\input [26]), .RegD(RegDst), .MemR(MemRead), .MemW(MemWrite));  // open: JrCt
  ir_2 ir_2_1 (
    .op1(\input [31]), .op2(\input [30]), .op3(\input [29]), .op4(\input [28]), .op5(\input [27]),
    .op6(\input [26]), .Branch(Branch), .Jmp(Jump), .RegWrite(ir_2_1_regwrite));
  ir_3 ir_3_1 (
    .op1(\input [31]), .op2(\input [30]), .op3(\input [29]), .op4(\input [28]), .op5(\input [27]),
    .op6(\input [26]), .MemTR(MemToReg), .AluSc(ir_3_1_alusc));
  ir_4 ir_4_1 (
    .op1(\input [31]), .op2(\input [30]), .op3(\input [29]), .op4(\input [28]), .op5(\input [27]),
    .op6(\input [26]), .AluOp0(ir_4_1_aluop2[2]), .AluOp1(ir_4_1_aluop2[1]), .AluOp2(ir_4_1_aluop2[0]));
  ir_jal ir_jal_1 (
    .op6(\input [31]), .op5(\input [30]), .op4(\input [29]), .op3(\input [28]), .op2(\input [27]),
    .op1(\input [26]), .out1(JAL));
  ir_jr ir_jr_1 (.op_code(\input [31:26]), .func(\input [5:0]), .jr(jr), .syscall(syscall));
  ir_interrupt ir_interrupt_1 (.in_1(\input ), .mfco(mfc0), .mtc0(mtc0), .eret(eret));
  ALU_circle alu_circle_1 (.alu_op(ir_4_1_aluop2), .func(\input [5:0]), .ALU_op_2(ALU_op), .src_r2(X_src_R2));
  or or_1 (AluSrc, ir_3_1_alusc, X_src_R2);
  and and_1 (RegWrite, ir_2_1_regwrite, ~eret, ~mtc0, ~jr);  // AND_Gate

  assign Branch_sel = \input [27:26];
  assign lh = \input [27];
endmodule

module ALU_circle (
  input  [2:0] alu_op,
  input  [5:0] func,
  output [3:0] ALU_op_2,
  output src_r2
);

  alu_1 alu_1_1 (
    .op3(alu_op[2]), .op2(alu_op[1]), .op1(alu_op[0]), .fun6(func[5]), .fun5(func[4]), .fun4(func[3]),
    .fun3(func[2]), .fun2(func[1]), .fun1(func[0]), .out4(ALU_op_2[3]), .out3(ALU_op_2[2]),
    .out2(ALU_op_2[1]), .out1(ALU_op_2[0]), .shift(src_r2));
endmodule

module ir_2 (
  input  op1,
  input  op2,
  input  op3,
  input  op4,
  input  op5,
  input  op6,
  output Branch,
  output Jmp,
  output RegWrite
);

  wire and_2_out, and_3_out, and_4_out, and_5_out, and_6_out, and_7_out, not_1_out, not_2_out, not_3_out,
       not_4_out, not_5_out, not_6_out, not_7_out, not_8_out, not_9_out, not_10_out, not_11_out, not_12_out,
       not_13_out;

  not not_1 (not_1_out, op3);
  not not_2 (not_2_out, op1);
  not not_3 (not_3_out, op3);
  not not_4 (not_4_out, op4);
  not not_5 (not_5_out, op1);
  not not_6 (not_6_out, op3);
  not not_7 (not_7_out, op1);
  not not_8 (not_8_out, op3);
  not not_9 (not_9_out, op4);
  not not_10 (not_10_out, op5);
  not not_11 (not_11_out, op3);
  not not_12 (not_12_out, op4);
  not not_13 (not_13_out, op1);
  and and_1 (Branch, not_1_out, op4);
  and and_2 (and_2_out, not_2_out, not_3_out, not_4_out, op5);
  and and_3 (and_3_out, not_5_out, not_6_out, op5, op6);
  and and_4 (and_4_out, not_7_out, op2, not_8_out, op5);
  and and_5 (and_5_out, not_9_out, not_10_out);
  and and_6 (and_6_out, not_11_out, not_12_out, op6);
  and and_7 (and_7_out, not_13_out, op3);
  or or_1 (Jmp, and_2_out, and_3_out, and_4_out);
  or or_2 (RegWrite, and_5_out, and_6_out, and_7_out);
endmodule

module ir_3 (
  input  op1,
  input  op2,
  input  op3,
  input  op4,
  input  op5,
  input  op6,
  output MemTR,
  output AluSc
);

  wire and_1_out, and_2_out, and_3_out, not_1_out;

  not not_1 (not_1_out, op2);
  and and_1 (and_1_out, op2, op4);
  and and_2 (and_2_out, op1, not_1_out, op6);
  and and_3 (and_3_out, op1, op4);
  or or_1 (AluSc, op5, op3, and_1_out, and_2_out, and_3_out);

  assign MemTR = op1;
endmodule

module ir_4 (
  input  op1,
  input  op2,
  input  op3,
  input  op4,
  input  op5,
  input  op6,
  output AluOp0,
  output AluOp1,
  output AluOp2
);

  wire and_2_out, and_3_out, and_4_out, and_5_out, and_6_out, and_7_out, and_8_out, not_1_out, not_2_out,
       not_3_out, not_4_out, not_5_out, not_6_out, not_7_out, not_8_out, not_9_out, not_10_out, not_11_out,
       not_12_out, not_13_out, not_14_out, not_15_out, not_16_out, not_17_out;

  not not_1 (not_1_out, op1);
  not not_2 (not_2_out, op2);
  not not_3 (not_3_out, op3);
  not not_4 (not_4_out, op5);
  not not_5 (not_5_out, op1);
  not not_6 (not_6_out, op2);
  not not_7 (not_7_out, op3);
  not not_8 (not_8_out, op6);
  not not_9 (not_9_out, op6);
  and and_1 (AluOp1, op3, op4);
  not not_10 (not_10_out, op2);
  not not_11 (not_11_out, op3);
  not not_12 (not_12_out, op5);
  not not_13 (not_13_out, op2);
  not not_14 (not_14_out, op3);
  not not_15 (not_15_out, op6);
  not not_16 (not_16_out, op4);
  not not_17 (not_17_out, op5);
  and and_2 (and_2_out, not_1_out, not_2_out, not_3_out, op4, not_4_out);
  and and_3 (and_3_out, not_5_out, not_6_out, not_7_out, op4, not_8_out);
  and and_4 (and_4_out, op3, op5, not_9_out);
  and and_5 (and_5_out, not_10_out, not_11_out, op4, not_12_out);
  and and_6 (and_6_out, not_13_out, not_14_out, op4, not_15_out);
  and and_7 (and_7_out, op3, not_16_out, not_17_out);
  and and_8 (and_8_out, op3, op6);
  or or_1 (AluOp0, and_2_out, and_3_out, and_4_out);
  or or_2 (AluOp2, and_5_out, and_6_out, and_7_out, and_8_out, op1);
endmodule

module ir_1 (
  input  op1,
  input  op2,
  input  op3,
  input  op4,
  input  op5,
  input  op6,
  output JrCt,
  output RegD,
  output MemR,
  output MemW
);

  wire and_2_out, and_3_out, and_4_out, and_5_out, not_1_out, not_2_out, not_3_out, not_4_out, not_5_out,
       not_6_out, not_7_out, not_8_out, not_9_out, not_10_out, not_11_out, not_12_out, not_13_out,
       not_14_out, not_15_out, not_16_out, not_17_out;

  not not_1 (not_1_out, op1);
  not not_2 (not_2_out, op2);
  not not_3 (not_3_out, op3);
  not not_4 (not_4_out, op4);
  not not_5 (not_5_out, op2);
  not not_6 (not_6_out, op3);
  not not_7 (not_7_out, op5);
  not not_8 (not_8_out, op6);
  not not_9 (not_9_out, op1);
  not not_10 (not_10_out, op3);
  not not_11 (not_11_out, op5);
  not not_12 (not_12_out, op3);
  not not_13 (not_13_out, op5);
  not not_14 (not_14_out, op3);
  not not_15 (not_15_out, op5);
  not not_16 (not_16_out, op2);
  not not_17 (not_17_out, op4);
  and and_1 (JrCt, not_1_out, not_2_out, not_3_out, not_4_out, op5, op6);
  and and_2 (and_2_out, not_5_out, not_6_out, not_7_out, not_8_out);
  and and_3 (and_3_out, not_9_out, not_10_out, not_11_out, op6);
  and and_4 (and_4_out, not_12_out, op4, not_13_out);
  and and_5 (and_5_out, op1, op2, not_14_out, not_15_out);
  and and_6 (MemW, op1, not_16_out, op3, not_17_out, op5, op6);
  or or_1 (RegD, and_2_out, and_3_out, and_4_out, and_5_out);

  assign MemR = op1;
endmodule

module alu_1 (
  input  op3,
  input  op2,
  input  op1,
  input  fun6,
  input  fun5,
  input  fun4,
  input  fun3,
  input  fun2,
  input  fun1,
  output out4,
  output out3,
  output out2,
  output out1,
  output shift
);

  wire and_1_out, and_2_out, and_3_out, and_4_out, and_5_out, and_6_out, and_7_out, and_8_out, and_9_out,
       and_10_out, and_11_out, and_12_out, and_13_out, and_14_out, and_15_out, and_16_out, and_17_out,
       and_18_out, and_19_out, and_20_out, and_21_out, and_22_out, and_23_out, and_24_out, and_25_out,
       and_26_out, not_1_out, not_2_out, not_3_out, not_4_out, not_5_out, not_6_out, not_7_out, not_8_out,
       not_9_out, not_10_out, not_11_out, not_12_out, not_13_out, not_14_out, not_15_out, not_16_out,
       not_17_out, not_18_out, not_19_out, not_20_out, not_21_out, not_22_out, not_23_out, not_24_out,
       not_25_out, not_26_out, not_27_out, not_28_out, not_29_out, not_30_out, not_31_out, not_32_out,
       not_33_out, not_34_out, not_35_out, not_36_out, not_37_out, not_38_out, not_39_out, not_40_out,
       not_41_out, not_42_out, not_43_out, not_44_out, not_45_out, not_46_out, not_47_out, not_48_out,
       not_49_out, not_50_out, not_51_out, not_52_out, not_53_out, not_54_out, not_55_out, not_56_out,
       not_57_out, not_58_out, not_59_out, not_60_out, not_61_out, not_62_out, not_63_out, not_64_out,
       not_65_out, or_1_out;

  not not_1 (not_1_out, op2);
  not not_2 (not_2_out, op1);
  not not_3 (not_3_out, fun6);
  not not_4 (not_4_out, fun5);
  not not_5 (not_5_out, fun2);
  not not_6 (not_6_out, op2);
  not not_7 (not_7_out, op1);
  not not_8 (not_8_out, op2);
  not not_9 (not_9_out, op1);
  not not_10 (not_10_out, op3);
  not not_11 (not_11_out, op2);
  not not_12 (not_12_out, fun1);
  not not_13 (not_13_out, op3);
  not not_14 (not_14_out, op2);
  not not_15 (not_15_out, fun6);
  not not_16 (not_16_out, fun5);
  not not_17 (not_17_out, fun4);
  not not_18 (not_18_out, op3);
  not not_19 (not_19_out, op2);
  not not_20 (not_20_out, fun4);
  not not_21 (not_21_out, fun3);
  not not_22 (not_22_out, op3);
  not not_23 (not_23_out, op2);
  not not_24 (not_24_out, fun5);
  not not_25 (not_25_out, fun3);
  not not_26 (not_26_out, op2);
  not not_27 (not_27_out, op1);
  not not_28 (not_28_out, op1);
  not not_29 (not_29_out, fun1);
  not not_30 (not_30_out, op1);
  not not_31 (not_31_out, op1);
  not not_32 (not_32_out, fun1);
  not not_33 (not_33_out, op1);
  not not_34 (not_34_out, fun1);
  not not_35 (not_35_out, op1);
  not not_36 (not_36_out, fun1);
  not not_37 (not_37_out, op1);
  not not_38 (not_38_out, op2);
  not not_39 (not_39_out, fun4);
  not not_40 (not_40_out, fun3);
  not not_41 (not_41_out, op2);
  not not_42 (not_42_out, fun5);
  not not_43 (not_43_out, fun2);
  not not_44 (not_44_out, fun1);
  not not_45 (not_45_out, op2);
  not not_46 (not_46_out, fun6);
  not not_47 (not_47_out, op2);
  not not_48 (not_48_out, fun2);
  not not_49 (not_49_out, op2);
  not not_50 (not_50_out, fun1);
  not not_51 (not_51_out, op2);
  not not_52 (not_52_out, op2);
  not not_53 (not_53_out, op2);
  not not_54 (not_54_out, fun2);
  not not_55 (not_55_out, fun1);
  not not_56 (not_56_out, op2);
  not not_57 (not_57_out, op1);
  not not_58 (not_58_out, fun1);
  and and_1 (and_1_out, not_1_out, not_2_out, not_3_out, not_4_out, fun3, not_5_out);
  and and_2 (and_2_out, not_6_out, not_7_out, fun3, fun1);
  and and_3 (and_3_out, not_8_out, not_9_out, fun4);
  and and_4 (and_4_out, op2, op1);
  and and_5 (and_5_out, not_10_out, not_11_out, fun3, not_12_out);
  and and_6 (and_6_out, not_13_out, not_14_out, not_15_out, not_16_out, not_17_out, fun3, fun2);
  and and_7 (and_7_out, not_18_out, not_19_out, fun6, not_20_out, not_21_out);
  and and_8 (and_8_out, not_22_out, not_23_out, fun6, not_24_out, not_25_out, fun2, fun1);
  and and_9 (and_9_out, not_26_out, op1);
  and and_10 (and_10_out, op2, not_27_out);
  and and_11 (and_11_out, not_28_out, fun2, not_29_out);
  and and_12 (and_12_out, not_30_out, fun3, fun2);
  and and_13 (and_13_out, not_31_out, fun4, fun3, not_32_out);
  and and_14 (and_14_out, not_33_out, fun5, fun3, not_34_out);
  and and_15 (and_15_out, not_35_out, fun6, fun3, not_36_out);
  and and_16 (and_16_out, op2, not_37_out);
  and and_17 (and_17_out, not_38_out, not_39_out, not_40_out, fun1);
  and and_18 (and_18_out, not_41_out, not_42_out, fun3, not_43_out, not_44_out);
  and and_19 (and_19_out, not_45_out, not_46_out, fun4);
  and and_20 (and_20_out, not_47_out, fun4, not_48_out);
  and and_21 (and_21_out, not_49_out, fun4, not_50_out);
  and and_22 (and_22_out, not_51_out, fun4, fun3);
  and and_23 (and_23_out, not_52_out, fun5, fun4);
  and and_24 (and_24_out, not_53_out, fun6, not_54_out, not_55_out);
  and and_25 (and_25_out, not_56_out, op1);
  and and_26 (and_26_out, op2, not_57_out);
  not not_59 (not_59_out, op3);
  not not_60 (not_60_out, op2);
  not not_61 (not_61_out, op1);
  not not_62 (not_62_out, fun6);
  not not_63 (not_63_out, fun5);
  not not_64 (not_64_out, fun4);
  not not_65 (not_65_out, fun3);
  or or_1 (or_1_out, fun2, not_58_out);
  or or_2 (out4, and_1_out, and_2_out, and_3_out, and_4_out, op3);
  or or_3 (out3, and_5_out, and_6_out, and_7_out, and_8_out, and_9_out, and_10_out);
  or or_4 (out2, and_11_out, and_12_out, and_13_out, and_14_out, and_15_out, and_16_out, op3);
  or or_5 (out1, and_17_out, and_18_out, and_19_out, and_20_out, and_21_out, and_22_out, and_23_out, and_24_out, and_25_out, and_26_out, op3);
  and and_27 (shift, not_59_out, not_60_out, not_61_out, not_62_out, not_63_out, not_64_out, not_65_out, or_1_out);
endmodule

module extender (
  input  [31:0] \input ,
  output [31:0] \output 
);

  wire [1:0] ext_ctrl_1_out1;
  wire [31:0] bit_extender_1_out, bit_extender_2_out, bit_extender_3_out;

  assign bit_extender_1_out = {{16{1'b0}}, \input [15:0]};  // Bit_Extender bit_extender_1
  assign bit_extender_2_out = {{16{\input [15]}}, \input [15:0]};  // Bit_Extender bit_extender_2
  assign bit_extender_3_out = {{27{\input [10]}}, \input [10:6]};  // Bit_Extender bit_extender_3
  ext_ctrl ext_ctrl_1 (
    .op6(\input [31]), .op5(\input [30]), .op4(\input [29]), .op3(\input [28]), .op2(\input [27]),
    .op1(\input [26]), .out2(ext_ctrl_1_out1[1]), .out1(ext_ctrl_1_out1[0]));
  Multiplexer #(.select(2), .width(32), .disabled(0), .enable("false")) multiplexer_1 (
    .in0(bit_extender_1_out), .in1(bit_extender_2_out), .in2(bit_extender_3_out), .out(\output ),
    .sel(ext_ctrl_1_out1));  // open: in3

  // Notes on the sheet:
  //   us[15:0]
  //   s[15:0]
  //   s[10:6]
endmodule

module ext_ctrl (
  input  op6,
  input  op5,
  input  op4,
  input  op3,
  input  op2,
  input  op1,
  output out2,
  output out1
);

  wire and_1_out, and_2_out, and_3_out, and_4_out, and_5_out, not_1_out, not_2_out, not_3_out, not_4_out,
       not_5_out, not_6_out, not_7_out, not_8_out, not_9_out, not_10_out, not_11_out, not_12_out, not_13_out,
       not_14_out;

  not not_1 (not_1_out, op6);
  not not_2 (not_2_out, op4);
  not not_3 (not_3_out, op3);
  not not_4 (not_4_out, op2);
  not not_5 (not_5_out, op4);
  not not_6 (not_6_out, op3);
  not not_7 (not_7_out, op2);
  not not_8 (not_8_out, op1);
  not not_9 (not_9_out, op4);
  not not_10 (not_10_out, op3);
  not not_11 (not_11_out, op2);
  not not_12 (not_12_out, op1);
  not not_13 (not_13_out, op5);
  not not_14 (not_14_out, op4);
  and and_1 (and_1_out, not_1_out, not_2_out, not_3_out, not_4_out);
  and and_2 (and_2_out, not_5_out, not_6_out, not_7_out, not_8_out);
  and and_3 (and_3_out, op5, not_9_out, not_10_out, not_11_out);
  and and_4 (and_4_out, op4, not_12_out);
  and and_5 (and_5_out, op6, not_13_out, not_14_out, op1);
  or or_1 (out2, and_1_out, and_2_out, and_3_out);
  or or_2 (out1, op2, op3, and_4_out, and_5_out);
endmodule

module ir_jal (
  input  op6,
  input  op5,
  input  op4,
  input  op3,
  input  op2,
  input  op1,
  output out1
);

  wire not_1_out, not_2_out;

  not not_1 (not_1_out, op2);
  not not_2 (not_2_out, op1);
  nor nor_1 (out1, not_1_out, not_2_out, op3, op4, op5, op6);
endmodule

module ir_jr (
  input  [5:0] op_code,
  input  [5:0] func,
  output jr,
  output syscall
);

  wire not_1_out, not_2_out, not_3_out, not_4_out, not_5_out, not_6_out, not_7_out, not_8_out, not_9_out,
       not_10_out, not_11_out;

  not not_1 (not_1_out, op_code[5]);
  not not_2 (not_2_out, op_code[4]);
  not not_3 (not_3_out, op_code[3]);
  not not_4 (not_4_out, op_code[2]);
  not not_5 (not_5_out, op_code[1]);
  not not_6 (not_6_out, op_code[0]);
  not not_7 (not_7_out, func[5]);
  not not_8 (not_8_out, func[4]);
  not not_9 (not_9_out, func[2]);
  not not_10 (not_10_out, func[1]);
  not not_11 (not_11_out, func[0]);
  and and_1 (jr, not_1_out, not_2_out, not_3_out, not_4_out, not_5_out, not_6_out, not_7_out, not_8_out, func[3], not_9_out, not_10_out, not_11_out);
  and and_2 (syscall, not_1_out, not_2_out, not_3_out, not_4_out, not_5_out, not_6_out, not_7_out, not_8_out, func[3], func[2], not_10_out, not_11_out);
endmodule

module wire_ir (
  input  [31:0] \input ,
  output [25:0] _25_0,
  output [15:0] _15_0,
  output [5:0] _31_26,
  output [4:0] _25_21,
  output [4:0] _20_16,
  output [4:0] _15_11,
  output [5:0] _5_0
);


  assign _5_0 = \input [5:0];
  assign _15_0 = \input [15:0];
  assign _15_11 = \input [15:11];
  assign _20_16 = \input [20:16];
  assign _25_0 = \input [25:0];
  assign _25_21 = \input [25:21];
  assign _31_26 = \input [31:26];
endmodule

module cp0 (
  input  [4:0] Reg1_num,
  input  [4:0] Write_Reg_num,
  input  [31:0] Din,
  input  [31:0] PC,
  input  Write_Enable,
  input  Clock,
  input  ERET,
  input  IR0,
  input  IR1,
  input  IR2,
  output [31:0] Reg1,
  output [31:0] NEW_PC,
  output out_13,
  output out_14,
  output out_15,
  output IS0,
  output IS1
);

  wire and_1_out, and_2_out, and_3_out, and_4_out, decoder_1_out0, decoder_1_out1, decoder_2_out1,
       decoder_2_out2, decoder_2_out3, not_1_out, or_1_out, or_2_out, or_3_out, or_4_out;
  wire [1:0] priority_encoder_1_out;
  wire [9:8] shift_register_1_out_5;
  wire [31:0] epc, IE_q, multiplexer_1_out, multiplexer_2_out;

  Decoder #(.disabled(0)) decoder_1 (
    .out0(decoder_1_out0), .out1(decoder_1_out1), .sel(Write_Reg_num[0]), .en(Write_Enable));
  Multiplexer #(.width(32), .disabled(0), .enable("false")) multiplexer_1 (
    .in0(Din), .in1(PC), .out(multiplexer_1_out), .sel(IS0));
  Multiplexer #(.width(32), .disabled(0), .enable("false")) multiplexer_2 (
    .in0(Din), .in1({32{1'b0}}), .out(multiplexer_2_out), .sel(IS0));
  or or_1 (or_1_out, decoder_1_out0, IS0);
  or or_2 (or_2_out, decoder_1_out1, IS0);
  // Probe on IE_q
  Register #(.width(32)) IE (.D(multiplexer_2_out), .en(or_1_out), .Q(IE_q), .clk(Clock));  // open: clr
  Register #(.width(32)) u_EPC (.D(multiplexer_1_out), .en(or_2_out), .Q(epc), .clk(Clock));  // open: clr
  // Probe on epc
  Multiplexer #(.width(32), .disabled(0), .enable("false")) multiplexer_3 (
    .in0(IE_q), .in1(epc), .out(Reg1), .sel(Reg1_num[0]));
  D_Flip_Flop d_ff_1 (.clk(IR0), .D(1'b1), .Q(out_13), .reset(decoder_2_out1));  // open: Qn, preset, en
  D_Flip_Flop d_ff_2 (.clk(IR1), .D(1'b1), .Q(out_14), .reset(decoder_2_out2));  // open: Qn, preset, en
  D_Flip_Flop d_ff_3 (.clk(IR2), .D(1'b1), .Q(out_15), .reset(decoder_2_out3));  // open: Qn, preset, en
  and and_1 (and_1_out, out_13, ~shift_register_1_out_5[8], ~shift_register_1_out_5[9]);  // AND_Gate
  and and_2 (and_2_out, out_14, ~shift_register_1_out_5[9]);  // AND_Gate
  and and_3 (and_3_out, out_15, ~and_4_out);  // AND_Gate
  and and_4 (and_4_out, shift_register_1_out_5[8], shift_register_1_out_5[9]);
  // Probe on priority_encoder_1_out
  Priority_Encoder #(.select(2)) priority_encoder_1 (
    .in0(1'b1), .in1(and_1_out), .in2(and_2_out), .in3(and_3_out), .out(priority_encoder_1_out));  // open: gs, en_out, en_in
  or or_3 (or_3_out, ERET, IS0);
  or or_4 (or_4_out, and_1_out, and_2_out, and_3_out);
  and and_5 (IS0, or_4_out, IE_q[0]);
  shift_register shift_register_1 (
    .left(ERET), .en(or_3_out), .\input (priority_encoder_1_out), .clk(Clock), .out_5(shift_register_1_out_5));
  D_Flip_Flop #(.trigger("falling")) d_ff_4 (.clk(IS0), .D(1'b1), .Q(IS1), .reset(not_1_out));  // open: Qn, preset, en
  not not_1 (not_1_out, Clock);
  Multiplexer #(.width(32), .enable("false")) multiplexer_4 (
    .in0({{22{1'b1}}, shift_register_1_out_5, {8{1'b0}}}), .in1(epc), .out(NEW_PC), .sel(ERET));
  // Probe on shift_register_1_out_5
  Decoder #(.select(2), .enable("false")) decoder_2 (
    .out1(decoder_2_out1), .out2(decoder_2_out2), .out3(decoder_2_out3), .sel(shift_register_1_out_5));  // open: out0

  // Other names for the same wires on the sheet: clk = Clock; WE = Write_Enable; write_data[31:0] = Din

  // Notes on the sheet:
  //   输入引脚
  //   输出引脚
endmodule

module test (
  input  in_1,
  input  in_2,
  input  [1:0] in_3,
  input  in_4,
  output [1:0] out_5
);

  wire and_1_out, button_1_out;
  wire [1:0] counter_1_q, shift_register_2_q1, shift_register_2_q2, shift_register_2_q3;

  Counter #(.width(2), .max('h3)) counter_1 (
    .count(in_2), .Q(counter_1_q), .clk(button_1_out), .clr(and_1_out));  // open: load, D, carry
  Button button_1 (.out(button_1_out));
  Shift_Register #(.width(32), .length(4)) shift_register_1 ();  // open: shift, in, clk, out, load, clr, d0, q0, d1, q1, d2, q2, d3, q3
  and and_1 (and_1_out, counter_1_q[0], counter_1_q[1]);
  Shift_Register #(.width(2), .length(4)) shift_register_2 (
    .in(in_3), .clk(in_4), .load(in_1), .d0(shift_register_2_q1), .q0(out_5), .d1(shift_register_2_q2),
    .q1(shift_register_2_q1), .d2(shift_register_2_q3), .q2(shift_register_2_q2), .d3(2'b00),
    .q3(shift_register_2_q3));  // open: shift, out, clr
endmodule

module ir_interrupt (
  input  [31:0] in_1,
  output mfco,
  output mtc0,
  output eret
);

  and and_1 (mfco, ~in_1[31], in_1[30], ~in_1[25], ~in_1[23]);  // AND_Gate
  and and_2 (mtc0, ~in_1[31], in_1[30], ~in_1[25], in_1[23]);  // AND_Gate
  and and_3 (eret, ~in_1[31], in_1[30], in_1[25], ~in_1[23]);  // AND_Gate
endmodule

module shift_register (
  input  left,
  input  en,
  input  [1:0] \input ,
  input  clk,
  output [1:0] out_5
);

  wire [1:0] shift_register_1_q1, shift_register_1_q2, shift_register_1_q3;

  Shift_Register #(.width(2), .length(4)) shift_register_1 (
    .shift(en), .in(\input ), .clk(clk), .load(left), .d0(shift_register_1_q1), .q0(out_5),
    .d1(shift_register_1_q2), .q1(shift_register_1_q1), .d2(shift_register_1_q3), .q2(shift_register_1_q2),
    .d3(2'b00), .q3(shift_register_1_q3));  // open: out, clr
endmodule

module CPU (
);

  wire alu_1_equal, AluSrc, and_2_out, and_3_out, Branch, clk, clock_1_out, comparator_1_eq, JAL, Jmp, JR,
       LH, lu, mem_we, MemRead, MemtoReg, MemWrite, multiplexer_4_out, not_1_out, not_2_out, not_3_out,
       RegWrite, syscall, XSrcR2;
  wire [1:0] BranchSel, ir_circle_1_branch_sel, priority_encoder_1_out;
  wire [3:0] AluOp, ir_circle_1_alu_op;
  wire [4:0] buffer_2_r1_num_2, buffer_2_r2_num_2, buffer_4_dst_2, ex_dst, mem_dst, multiplexer_1_out;
  wire [9:0] buffer_3_alu_r_2_2;
  wire [15:0] multiplexer_6_out;
  wire [21:0] ir_circle_1_branch;
  wire [29:0] bit_extender_1_out;
  wire [31:0] adder_1_out, adder_2_out, alu_1_result, and_1_out, bit_extender_2_out, buffer_1_ir_2,
       buffer_1_pc_2, buffer_2_a0_2, buffer_2_ext_2, buffer_2_ir_2, buffer_2_pc_2, buffer_2_r1_2,
       buffer_2_r2_2, buffer_2_signal_2, buffer_2_v0_2, buffer_3_a0_2, buffer_3_alu_r_2, buffer_3_ir_2,
       buffer_3_pc_2, buffer_3_r2_2, buffer_3_signal_2, buffer_3_v0_2, buffer_4_a0_2, buffer_4_alu_r_2,
       buffer_4_d_2, buffer_4_ir_2, buffer_4_pc_2, buffer_4_signal_2, buffer_4_v0_2, display,
       extender_1_output, main_1_a0_value, main_1_reg1, main_1_reg2_2, main_1_v0_value, multiplexer_2_out,
       multiplexer_3_out, multiplexer_5_out, multiplexer_7_out, multiplexer_8_out, PC_q, ram_1_data,
       redirect_1_out_9, redirect_2_out_9, redirect_3_out_9, redirect_4_out_9, rom_1_data;

  not not_1 (not_1_out, lu);
  Register #(.width(32), .trigger("falling")) PC (.D(adder_1_out), .en(not_1_out), .Q(PC_q), .clk(clk), .clr(1'b0));
  Counter counter_1 (.clk(clk));  // open: load, D, count, Q, carry, clr
  Adder #(.width(32)) adder_1 (.a(32'h4), .b(PC_q), .out(adder_1_out));  // open: cin, cout
  ROM #(.addrWidth(10), .dataWidth(32)) rom_1 (.addr(PC_q[11:2]), .data(rom_1_data), .sel(1'b1));
  // Probe on buffer_1_pc_2
  buffer buffer_1 (
    .PC(adder_1_out), .IR(rom_1_data), .PC_2(buffer_1_pc_2), .IR_2(buffer_1_ir_2), .in_15(clk), .en(not_2_out));  // open: signal, R1, R2, ALU_R, v0, a0, signal_2, R1_2, R2_2, ALU_R_2, v0_2, a0_2, cp0, cp0_2, D, D_2, ext, ext_2, dst, dst_2, R1_num, R1_num_2, R2_num, R2_num_2
  not not_2 (not_2_out, lu);
  // Probe on buffer_1_ir_2
  IR_circle ir_circle_1 (
    .\input (buffer_1_ir_2), .RegDst(ir_circle_1_branch[0]), .Branch(ir_circle_1_branch[1]),
    .Jump(ir_circle_1_branch[2]), .MemToReg(ir_circle_1_branch[3]), .MemRead(ir_circle_1_branch[4]),
    .MemWrite(ir_circle_1_branch[5]), .AluSrc(ir_circle_1_branch[6]), .RegWrite(ir_circle_1_branch[7]),
    .ALU_op(ir_circle_1_alu_op), .X_src_R2(ir_circle_1_branch[12]), .JAL(ir_circle_1_branch[13]),
    .jr(ir_circle_1_branch[14]), .syscall(ir_circle_1_branch[15]), .mfc0(ir_circle_1_branch[16]),
    .mtc0(ir_circle_1_branch[17]), .eret(ir_circle_1_branch[18]), .Branch_sel(ir_circle_1_branch_sel),
    .lh(ir_circle_1_branch[21]));
  assign and_1_out = ~{32{lu}} & {{10{1'b0}}, ir_circle_1_branch[21], ir_circle_1_branch_sel, ir_circle_1_branch[18:12], ir_circle_1_alu_op, ir_circle_1_branch[7:0]};  // AND_Gate and_1, 32 bits wide
  extender extender_1 (.\input (buffer_1_ir_2), .\output (extender_1_output));
  regfile_main main_1 (
    .Reg1_num(buffer_1_ir_2[25:21]), .Reg2(buffer_1_ir_2[20:16]), .Write_Reg_num(buffer_4_dst_2),
    .Din(multiplexer_8_out), .Write_Enable(RegWrite), .Clock(clk), .Reg1(main_1_reg1),
    .Reg2_2(main_1_reg2_2), .v0_Value(main_1_v0_value), .a0_Value(main_1_a0_value));  // open: s2_Value, ra_Value
  Multiplexer #(.select(2), .width(5), .disabled(0), .enable("false")) multiplexer_1 (
    .in0(buffer_1_ir_2[20:16]), .in1(buffer_1_ir_2[15:11]), .in2({5{1'b1}}), .in3({5{1'b1}}),
    .out(multiplexer_1_out), .sel({ir_circle_1_branch[13], ir_circle_1_branch[0]}));
  buffer buffer_2 (
    .PC(buffer_1_pc_2), .IR(buffer_1_ir_2), .signal(and_1_out), .R1(main_1_reg1), .R2(main_1_reg2_2),
    .v0(main_1_v0_value), .a0(main_1_a0_value), .PC_2(buffer_2_pc_2), .IR_2(buffer_2_ir_2),
    .signal_2({buffer_2_signal_2[31:21], BranchSel, buffer_2_signal_2[18:15], JR, buffer_2_signal_2[13], XSrcR2, AluOp, buffer_2_signal_2[7], AluSrc, buffer_2_signal_2[5:3], Jmp, Branch, buffer_2_signal_2[0]}),
    .R1_2(buffer_2_r1_2), .R2_2(buffer_2_r2_2), .v0_2(buffer_2_v0_2), .a0_2(buffer_2_a0_2), .in_15(clk),
    .ext(extender_1_output), .ext_2(buffer_2_ext_2), .dst(multiplexer_1_out), .dst_2(ex_dst),
    .R1_num(buffer_1_ir_2[25:21]), .R1_num_2(buffer_2_r1_num_2), .R2_num(buffer_1_ir_2[20:16]),
    .R2_num_2(buffer_2_r2_num_2), .en(1'b1));  // open: ALU_R, ALU_R_2, cp0, cp0_2, D, D_2
  load_use load_use_1 (
    .syscall(ir_circle_1_branch[15]), .R1_num(buffer_1_ir_2[25:21]), .R2_num(buffer_1_ir_2[20:16]), .lu(lu),
    .in_4(buffer_2_r2_num_2), .MemRead(buffer_2_signal_2[4]));
  // Probe on buffer_2_pc_2
  // Probe on buffer_2_ir_2
  redirect redirect_1 (
    .\input (buffer_2_r1_2), .input_dst(buffer_2_r1_num_2), .wb_data(multiplexer_8_out),
    .wb_dst(buffer_4_dst_2), .wb_we(RegWrite),
    .mem_data({buffer_3_alu_r_2[31:12], buffer_3_alu_r_2_2, buffer_3_alu_r_2[1:0]}), .mem_dst(mem_dst),
    .mem_we(mem_we), .out_9(redirect_1_out_9));
  redirect redirect_2 (
    .\input (buffer_2_r2_2), .input_dst(buffer_2_r2_num_2), .wb_data(multiplexer_8_out),
    .wb_dst(buffer_4_dst_2), .wb_we(RegWrite),
    .mem_data({buffer_3_alu_r_2[31:12], buffer_3_alu_r_2_2, buffer_3_alu_r_2[1:0]}), .mem_dst(mem_dst),
    .mem_we(mem_we), .out_9(redirect_2_out_9));
  redirect redirect_3 (
    .\input (buffer_2_v0_2), .input_dst(5'b00010), .wb_data(multiplexer_8_out), .wb_dst(buffer_4_dst_2),
    .wb_we(RegWrite), .mem_data({buffer_3_alu_r_2[31:12], buffer_3_alu_r_2_2, buffer_3_alu_r_2[1:0]}),
    .mem_dst(mem_dst), .mem_we(mem_we), .out_9(redirect_3_out_9));
  redirect redirect_4 (
    .\input (buffer_2_a0_2), .input_dst(5'b00100), .wb_data(multiplexer_8_out), .wb_dst(buffer_4_dst_2),
    .wb_we(RegWrite), .mem_data({buffer_3_alu_r_2[31:12], buffer_3_alu_r_2_2, buffer_3_alu_r_2[1:0]}),
    .mem_dst(mem_dst), .mem_we(mem_we), .out_9(redirect_4_out_9));
  assign bit_extender_1_out = {{14{buffer_2_ir_2[15]}}, buffer_2_ir_2[15:0]};  // Bit_Extender bit_extender_1
  Multiplexer #(.width(32), .enable("false")) multiplexer_2 (
    .in0(redirect_1_out_9), .in1(redirect_2_out_9), .out(multiplexer_2_out), .sel(XSrcR2));
  Multiplexer #(.width(32), .enable("false")) multiplexer_3 (
    .in0(redirect_2_out_9), .in1(buffer_2_ext_2), .out(multiplexer_3_out), .sel(AluSrc));
  ALU alu_1 (
    .AluOP(AluOp), .X(multiplexer_2_out), .Equal(alu_1_equal), .Result(alu_1_result), .Y(multiplexer_3_out));  // open: Signed_Overflow, Result_2, UnSigned_Overflow
  Adder #(.width(32)) adder_2 (
    .a(buffer_2_pc_2), .b({bit_extender_1_out, 2'b00}), .out(adder_2_out));  // open: cin, cout
  Multiplexer #(.select(2), .disabled(0)) multiplexer_4 (
    .in0(alu_1_equal), .in1(not_3_out), .in2(alu_1_result[0]), .out(multiplexer_4_out), .sel(BranchSel),
    .en(Branch));  // open: in3
  not not_3 (not_3_out, alu_1_equal);
  Multiplexer #(.select(2), .width(32), .disabled(0), .enable("false")) multiplexer_5 (
    .in0(buffer_2_pc_2), .in1(adder_2_out), .in2({buffer_2_pc_2[31:28], buffer_2_ir_2[25:0], 2'b00}),
    .in3(redirect_1_out_9), .out(multiplexer_5_out), .sel(priority_encoder_1_out));
  Priority_Encoder #(.select(2)) priority_encoder_1 (
    .in0(1'b1), .in1(multiplexer_4_out), .in2(Jmp), .in3(JR), .out(priority_encoder_1_out));  // open: gs, en_out, en_in
  buffer buffer_3 (
    .PC(buffer_2_pc_2), .IR(buffer_2_ir_2),
    .signal({buffer_2_signal_2[31:21], BranchSel, buffer_2_signal_2[18:15], JR, buffer_2_signal_2[13], XSrcR2, AluOp, buffer_2_signal_2[7], AluSrc, buffer_2_signal_2[5:3], Jmp, Branch, buffer_2_signal_2[0]}),
    .R1(redirect_1_out_9), .R2(redirect_2_out_9), .ALU_R(alu_1_result), .v0(redirect_3_out_9),
    .a0(redirect_4_out_9), .PC_2(buffer_3_pc_2), .IR_2(buffer_3_ir_2),
    .signal_2({buffer_3_signal_2[31:22], LH, buffer_3_signal_2[20:8], mem_we, buffer_3_signal_2[6], MemWrite, MemRead, buffer_3_signal_2[3:0]}),
    .R2_2(buffer_3_r2_2), .ALU_R_2({buffer_3_alu_r_2[31:12], buffer_3_alu_r_2_2, buffer_3_alu_r_2[1:0]}),
    .v0_2(buffer_3_v0_2), .a0_2(buffer_3_a0_2), .in_15(clk), .dst(ex_dst), .dst_2(mem_dst), .en(1'b1));  // open: R1_2, cp0, cp0_2, D, D_2, ext, ext_2, R1_num, R1_num_2, R2_num, R2_num_2
  // Probe on buffer_3_ir_2
  // Probe on buffer_3_pc_2
  RAM #(.addrWidth(10), .dataWidth(32), .bus("separate")) ram_1 (
    .addr(buffer_3_alu_r_2_2), .din(buffer_3_r2_2), .data(ram_1_data), .str(MemWrite), .clk(clk), .ld(MemRead));  // open: sel, clr
  Multiplexer #(.width(16), .disabled(0), .enable("false")) multiplexer_6 (
    .in0(ram_1_data[15:0]), .in1(ram_1_data[31:16]), .out(multiplexer_6_out), .sel(buffer_3_alu_r_2[1]));
  Multiplexer #(.width(32), .disabled(0), .enable("false")) multiplexer_7 (
    .in0(ram_1_data), .in1(bit_extender_2_out), .out(multiplexer_7_out), .sel(LH));
  assign bit_extender_2_out = {{16{multiplexer_6_out[15]}}, multiplexer_6_out};  // Bit_Extender bit_extender_2
  buffer buffer_4 (
    .PC(buffer_3_pc_2), .IR(buffer_3_ir_2),
    .signal({buffer_3_signal_2[31:22], LH, buffer_3_signal_2[20:8], mem_we, buffer_3_signal_2[6], MemWrite, MemRead, buffer_3_signal_2[3:0]}),
    .ALU_R({buffer_3_alu_r_2[31:12], buffer_3_alu_r_2_2, buffer_3_alu_r_2[1:0]}), .v0(buffer_3_v0_2),
    .a0(buffer_3_a0_2), .PC_2(buffer_4_pc_2), .IR_2(buffer_4_ir_2),
    .signal_2({buffer_4_signal_2[31:16], syscall, buffer_4_signal_2[14], JAL, buffer_4_signal_2[12:8], RegWrite, buffer_4_signal_2[6:4], MemtoReg, buffer_4_signal_2[2:0]}),
    .ALU_R_2(buffer_4_alu_r_2), .v0_2(buffer_4_v0_2), .a0_2(buffer_4_a0_2), .in_15(clk),
    .D(multiplexer_7_out), .D_2(buffer_4_d_2), .dst(mem_dst), .dst_2(buffer_4_dst_2), .en(1'b1));  // open: R1, R2, R1_2, R2_2, cp0, cp0_2, ext, ext_2, R1_num, R1_num_2, R2_num, R2_num_2
  // Probe on buffer_4_ir_2
  // Probe on buffer_4_pc_2
  Comparator #(.width(32)) comparator_1 (.a(buffer_4_v0_2), .b(32'ha), .eq(comparator_1_eq));  // open: gt, lt
  Multiplexer #(.select(2), .width(32), .enable("false")) multiplexer_8 (
    .in0(buffer_4_alu_r_2), .in1(buffer_4_d_2), .in2(buffer_4_pc_2), .in3(buffer_4_pc_2),
    .out(multiplexer_8_out), .sel({JAL, MemtoReg}));
  Clock clock_1 (.out(clock_1_out));
  and and_2 (and_2_out, comparator_1_eq, syscall);
  and and_3 (and_3_out, ~comparator_1_eq, syscall);  // AND_Gate
  and and_4 (clk, clock_1_out, ~and_2_out);  // AND_Gate
  Register #(.width(32)) register_1 (.D(buffer_4_a0_2), .en(and_3_out), .Q(display));  // open: clk, clr

  // Notes on the sheet:
  //   contents of rom_1 (hex, n*v repeats v):
  //   20110004 ae310000 8e320000 2252fffc 20100000 22110001 2118020 22520004 ae500000 22310001 2118020
  //   22520004 ae500000 22310001 2118020 22520004 ae500000 22310001 2118020 22520004 ae500000 22310001
  //   2118020 22520004 ae500000 22310001 2118020 22520004 ae500000 22310001 2118020 22520004 ae500000
  //   2002000a 20100000 20100000 20100000 c
endmodule

module buffer (
  input  [31:0] PC,
  input  [31:0] IR,
  input  [31:0] signal,
  input  [4:0] dst,
  input  [4:0] R1_num,
  input  [4:0] R2_num,
  input  [31:0] D,
  input  [31:0] cp0,
  input  [31:0] R1,
  input  [31:0] R2,
  input  [31:0] ALU_R,
  input  [31:0] ext,
  input  [31:0] v0,
  input  [31:0] a0,
  input  in_15,
  input  en,
  output [31:0] PC_2,
  output [31:0] IR_2,
  output [31:0] signal_2,
  output [4:0] dst_2,
  output [4:0] R1_num_2,
  output [4:0] R2_num_2,
  output [31:0] D_2,
  output [31:0] cp0_2,
  output [31:0] R1_2,
  output [31:0] R2_2,
  output [31:0] ALU_R_2,
  output [31:0] ext_2,
  output [31:0] v0_2,
  output [31:0] a0_2
);

  Register #(.width(32)) register_1 (.D(PC), .en(en), .Q(PC_2), .clk(in_15));  // open: clr
  Register #(.width(32)) register_2 (.D(IR), .en(en), .Q(IR_2), .clk(in_15));  // open: clr
  Register #(.width(32)) register_3 (.D(signal), .en(en), .Q(signal_2), .clk(in_15));  // open: clr
  Register #(.width(5)) u_dst (.D(dst), .en(en), .Q(dst_2), .clk(in_15));  // open: clr
  Register #(.width(5)) u_R1_num (.D(R1_num), .en(en), .Q(R1_num_2), .clk(in_15));  // open: clr
  Register #(.width(5)) u_R2_num (.D(R2_num), .en(en), .Q(R2_num_2), .clk(in_15));  // open: clr
  Register #(.width(32)) register_4 (.D(D), .en(en), .Q(D_2), .clk(in_15));  // open: clr
  Register #(.width(32)) register_5 (.D(cp0), .en(en), .Q(cp0_2), .clk(in_15));  // open: clr
  Register #(.width(32)) register_6 (.D(R1), .en(en), .Q(R1_2), .clk(in_15));  // open: clr
  Register #(.width(32)) register_7 (.D(R2), .en(en), .Q(R2_2), .clk(in_15));  // open: clr
  Register #(.width(32)) register_8 (.D(ALU_R), .en(en), .Q(ALU_R_2), .clk(in_15));  // open: clr
  Register #(.width(32)) u_ext (.D(ext), .en(en), .Q(ext_2), .clk(in_15));  // open: clr
  Register #(.width(32)) register_9 (.D(v0), .en(en), .Q(v0_2), .clk(in_15));  // open: clr
  Register #(.width(32)) register_10 (.D(a0), .en(en), .Q(a0_2), .clk(in_15));  // open: clr
endmodule

module hazard_unit (
  input  ex_en,
  input  [4:0] ex_dst,
  input  mem_en,
  input  [4:0] mem_dst,
  input  [31:0] ex_result,
  input  [31:0] mem_result,
  output [31:0] result,
  output [4:0] dst,
  output en
);

  or or_1 (en, ex_en, mem_en);
  Multiplexer #(.width(5), .enable("false")) multiplexer_1 (.in0(mem_dst), .in1(ex_dst), .out(dst), .sel(ex_en));
  Multiplexer #(.width(32), .enable("false")) multiplexer_2 (
    .in0(mem_result), .in1(ex_result), .out(result), .sel(ex_en));
endmodule

module redirect (
  input  [31:0] \input ,
  input  [4:0] input_dst,
  input  [31:0] wb_data,
  input  [4:0] wb_dst,
  input  wb_we,
  input  [31:0] mem_data,
  input  [4:0] mem_dst,
  input  mem_we,
  output [31:0] out_9
);

  wire and_1_out, and_2_out, comparator_1_eq, comparator_2_eq;
  wire [31:0] multiplexer_1_out;

  Comparator #(.width(5)) comparator_1 (.a(input_dst), .b(wb_dst), .eq(comparator_1_eq));  // open: gt, lt
  Comparator #(.width(5)) comparator_2 (.a(input_dst), .b(mem_dst), .eq(comparator_2_eq));  // open: gt, lt
  Multiplexer #(.width(32), .enable("false")) multiplexer_1 (
    .in0(\input ), .in1(wb_data), .out(multiplexer_1_out), .sel(and_1_out));
  and and_1 (and_1_out, comparator_1_eq, wb_we);
  Multiplexer #(.width(32), .enable("false")) multiplexer_2 (
    .in0(multiplexer_1_out), .in1(mem_data), .out(out_9), .sel(and_2_out));
  and and_2 (and_2_out, comparator_2_eq, mem_we);
endmodule

module load_use (
  input  syscall,
  input  [4:0] R1_num,
  input  [4:0] R2_num,
  input  [4:0] in_4,
  input  MemRead,
  output lu
);

  wire and_1_out, comparator_1_eq, comparator_2_eq, comparator_3_eq, comparator_4_eq, or_1_out, or_2_out;

  Comparator #(.width(5)) comparator_1 (.a(5'b00010), .b(in_4), .eq(comparator_1_eq));  // open: gt, lt
  Comparator #(.width(5)) comparator_2 (.a(5'b00100), .b(in_4), .eq(comparator_2_eq));  // open: gt, lt
  Comparator #(.width(5)) comparator_3 (.a(R1_num), .b(in_4), .eq(comparator_3_eq));  // open: gt, lt
  Comparator #(.width(5)) comparator_4 (.a(R2_num), .b(in_4), .eq(comparator_4_eq));  // open: gt, lt
  or or_1 (or_1_out, comparator_1_eq, comparator_2_eq);
  and and_1 (and_1_out, syscall, or_1_out);
  or or_2 (or_2_out, and_1_out, comparator_3_eq, comparator_4_eq);
  and and_2 (lu, or_2_out, MemRead);
endmodule
