// Logisim project regfile.circ as structural Verilog: 1 circuit, main circuit main
module main (
  input  [4:0] Reg1_num,
  input  [4:0] Reg2,
  input  [4:0] Write_Reg_num,
  input  [31:0] Din,
  input  Write_Enable,
  input  Clock,
  output [31:0] Reg1,
  output [31:0] v0_Value,
  output [31:0] a0_Value,
  output [31:0] s2_Value,
  output [31:0] ra_Value,
  output [31:0] Reg2_2
);

  wire decoder_1_out0, decoder_1_out1, decoder_1_out2, decoder_1_out3, decoder_1_out4, decoder_1_out5,
       decoder_1_out6, decoder_1_out7, decoder_1_out8, decoder_1_out9, decoder_1_out10, decoder_1_out11,
       decoder_1_out12, decoder_1_out13, decoder_1_out14, decoder_1_out15, decoder_1_out16, decoder_1_out17,
       decoder_1_out18, decoder_1_out19, decoder_1_out20, decoder_1_out21, decoder_1_out22, decoder_1_out23,
       decoder_1_out24, decoder_1_out25, decoder_1_out26, decoder_1_out27, decoder_1_out28, decoder_1_out29,
       decoder_1_out30, decoder_1_out31;
  wire [31:0] _0_q, _1_q, _3_q, _5_q, _6_q, _7_q, _8_q, _9_q, _10_q, _11_q, _12_q, _13_q, _14_q, _15_q,
       _16_q, _17_q, _19_q, _20_q, _21_q, _22_q, _23_q, _24_q, _25_q, _26_q, _27_q, _28_q, _29_q, _30_q;

  Decoder #(.select(5), .disabled(0)) decoder_1 (
    .out0(decoder_1_out0), .out1(decoder_1_out1), .out2(decoder_1_out2), .out3(decoder_1_out3),
    .out4(decoder_1_out4), .out5(decoder_1_out5), .out6(decoder_1_out6), .out7(decoder_1_out7),
    .out8(decoder_1_out8), .out9(decoder_1_out9), .out10(decoder_1_out10), .out11(decoder_1_out11),
    .out12(decoder_1_out12), .out13(decoder_1_out13), .out14(decoder_1_out14), .out15(decoder_1_out15),
    .out16(decoder_1_out16), .out17(decoder_1_out17), .out18(decoder_1_out18), .out19(decoder_1_out19),
    .out20(decoder_1_out20), .out21(decoder_1_out21), .out22(decoder_1_out22), .out23(decoder_1_out23),
    .out24(decoder_1_out24), .out25(decoder_1_out25), .out26(decoder_1_out26), .out27(decoder_1_out27),
    .out28(decoder_1_out28), .out29(decoder_1_out29), .out30(decoder_1_out30), .out31(decoder_1_out31),
    .sel(Write_Reg_num), .en(Write_Enable));
  Register #(.width(32), .trigger("falling")) _0 (.D(Din), .en(decoder_1_out0), .Q(_0_q), .clk(Clock), .clr(1'b1));
  Register #(.width(32), .trigger("falling")) _4 (
    .D(Din), .en(decoder_1_out4), .Q(a0_Value), .clk(Clock));  // open: clr
  Register #(.width(32), .trigger("falling")) _8 (.D(Din), .en(decoder_1_out8), .Q(_8_q), .clk(Clock));  // open: clr
  Register #(.width(32), .trigger("falling")) _12 (.D(Din), .en(decoder_1_out12), .Q(_12_q), .clk(Clock));  // open: clr
  Register #(.width(32), .trigger("falling")) _16 (.D(Din), .en(decoder_1_out16), .Q(_16_q), .clk(Clock));  // open: clr
  Register #(.width(32), .trigger("falling")) _20 (.D(Din), .en(decoder_1_out20), .Q(_20_q), .clk(Clock));  // open: clr
  Register #(.width(32), .trigger("falling")) _24 (.D(Din), .en(decoder_1_out24), .Q(_24_q), .clk(Clock));  // open: clr
  Register #(.width(32), .trigger("falling")) _28 (.D(Din), .en(decoder_1_out28), .Q(_28_q), .clk(Clock));  // open: clr
  Register #(.width(32), .trigger("falling")) _1 (.D(Din), .en(decoder_1_out1), .Q(_1_q), .clk(Clock));  // open: clr
  Register #(.width(32), .trigger("falling")) _5 (.D(Din), .en(decoder_1_out5), .Q(_5_q), .clk(Clock));  // open: clr
  Register #(.width(32), .trigger("falling")) _9 (.D(Din), .en(decoder_1_out9), .Q(_9_q), .clk(Clock));  // open: clr
  Register #(.width(32), .trigger("falling")) _13 (.D(Din), .en(decoder_1_out13), .Q(_13_q), .clk(Clock));  // open: clr
  Register #(.width(32), .trigger("falling")) _17 (.D(Din), .en(decoder_1_out17), .Q(_17_q), .clk(Clock));  // open: clr
  Register #(.width(32), .trigger("falling")) _21 (.D(Din), .en(decoder_1_out21), .Q(_21_q), .clk(Clock));  // open: clr
  Register #(.width(32), .trigger("falling")) _25 (.D(Din), .en(decoder_1_out25), .Q(_25_q), .clk(Clock));  // open: clr
  Register #(.width(32), .trigger("falling")) _29 (.D(Din), .en(decoder_1_out29), .Q(_29_q), .clk(Clock));  // open: clr
  Register #(.width(32), .trigger("falling")) _2 (
    .D(Din), .en(decoder_1_out2), .Q(v0_Value), .clk(Clock));  // open: clr
  Register #(.width(32), .trigger("falling")) _6 (.D(Din), .en(decoder_1_out6), .Q(_6_q), .clk(Clock));  // open: clr
  Register #(.width(32), .trigger("falling")) _10 (.D(Din), .en(decoder_1_out10), .Q(_10_q), .clk(Clock));  // open: clr
  Register #(.width(32), .trigger("falling")) _14 (.D(Din), .en(decoder_1_out14), .Q(_14_q), .clk(Clock));  // open: clr
  Register #(.width(32), .trigger("falling")) _18 (
    .D(Din), .en(decoder_1_out18), .Q(s2_Value), .clk(Clock));  // open: clr
  Register #(.width(32), .trigger("falling")) _22 (.D(Din), .en(decoder_1_out22), .Q(_22_q), .clk(Clock));  // open: clr
  Register #(.width(32), .trigger("falling")) _26 (.D(Din), .en(decoder_1_out26), .Q(_26_q), .clk(Clock));  // open: clr
  Register #(.width(32), .trigger("falling")) _30 (.D(Din), .en(decoder_1_out30), .Q(_30_q), .clk(Clock));  // open: clr
  Register #(.width(32), .trigger("falling")) _3 (.D(Din), .en(decoder_1_out3), .Q(_3_q), .clk(Clock));  // open: clr
  Register #(.width(32), .trigger("falling")) _7 (.D(Din), .en(decoder_1_out7), .Q(_7_q), .clk(Clock));  // open: clr
  Register #(.width(32), .trigger("falling")) _11 (.D(Din), .en(decoder_1_out11), .Q(_11_q), .clk(Clock));  // open: clr
  Register #(.width(32), .trigger("falling")) _15 (.D(Din), .en(decoder_1_out15), .Q(_15_q), .clk(Clock));  // open: clr
  Register #(.width(32), .trigger("falling")) _19 (.D(Din), .en(decoder_1_out19), .Q(_19_q), .clk(Clock));  // open: clr
  Register #(.width(32), .trigger("falling")) _23 (.D(Din), .en(decoder_1_out23), .Q(_23_q), .clk(Clock));  // open: clr
  Register #(.width(32), .trigger("falling")) _27 (.D(Din), .en(decoder_1_out27), .Q(_27_q), .clk(Clock));  // open: clr
  Register #(.width(32), .trigger("falling")) _31 (
    .D(Din), .en(decoder_1_out31), .Q(ra_Value), .clk(Clock));  // open: clr
  Multiplexer #(.select(5), .width(32), .disabled(0), .enable("false")) multiplexer_1 (
    .in0(_0_q), .in1(_1_q), .in2(v0_Value), .in3(_3_q), .in4(a0_Value), .in5(_5_q), .in6(_6_q), .in7(_7_q),
    .in8(_8_q), .in9(_9_q), .in10(_10_q), .in11(_11_q), .in12(_12_q), .in13(_13_q), .in14(_14_q),
    .in15(_15_q), .in16(_16_q), .in17(_17_q), .in18(s2_Value), .in19(_19_q), .in20(_20_q), .in21(_21_q),
    .in22(_22_q), .in23(_23_q), .in24(_24_q), .in25(_25_q), .in26(_26_q), .in27(_27_q), .in28(_28_q),
    .in29(_29_q), .in30(_30_q), .in31(ra_Value), .out(Reg2_2), .sel(Reg2));
  Multiplexer #(.select(5), .width(32), .disabled(0), .enable("false")) multiplexer_2 (
    .in0(_0_q), .in1(_1_q), .in2(v0_Value), .in3(_3_q), .in4(a0_Value), .in5(_5_q), .in6(_6_q), .in7(_7_q),
    .in8(_8_q), .in9(_9_q), .in10(_10_q), .in11(_11_q), .in12(_12_q), .in13(_13_q), .in14(_14_q),
    .in15(_15_q), .in16(_16_q), .in17(_17_q), .in18(s2_Value), .in19(_19_q), .in20(_20_q), .in21(_21_q),
    .in22(_22_q), .in23(_23_q), .in24(_24_q), .in25(_25_q), .in26(_26_q), .in27(_27_q), .in28(_28_q),
    .in29(_29_q), .in30(_30_q), .in31(ra_Value), .out(Reg1), .sel(Reg1_num));

  // Other names for the same wires on the sheet: a0[31:0] = a0_Value; clk = Clock; ra[31:0] = ra_Value;
  //   reg2_num[4:0] = Reg2; reg2_t[31:0] = Reg2_2; s2[31:0] = s2_Value; v0[31:0] = v0_Value; WE = Write_Enable;
  //   write_data[31:0] = Din

  // Notes on the sheet:
  //   输入引脚
  //   输出引脚
  //   Debug引脚，便于观测寄存器值
  //   请勿修改引脚以及封装，直接使用隧道连接电路
endmodule
